// Logisim project ASS 3.circ as structural Verilog: 1 circuit, main circuit main
module main (
  input  A,
  input  B,
  input  F
);

  wire and_1_out, and_2_out, or_1_out, undriven, undriven_2;

  and and_1 (and_1_out, undriven, ~undriven_2);  // AND_Gate
  and and_2 (and_2_out, ~undriven, undriven_2);  // AND_Gate
  or or_1 (or_1_out, and_1_out, and_2_out);
endmodule
