// Logisim project Ass4.circ as structural Verilog: 1 circuit, main circuit main
module main (
  input  a,
  input  b,
  input  c,
  input  d
);

  wire and_1_out, and_2_out, and_3_out, and_4_out, or_1_out;

  and and_1 (and_1_out, a, b);
  and and_2 (and_2_out, a, ~c);  // AND_Gate
  and and_3 (and_3_out, b, ~c);  // AND_Gate
  and and_4 (and_4_out, b, ~c, ~d);  // AND_Gate
  LED z (.in(or_1_out));
  or or_1 (or_1_out, and_1_out, and_2_out, and_3_out, and_4_out);
endmodule
