// Logisim project ass5.circ as structural Verilog: 1 circuit, main circuit main
module main (
  input  W,
  input  E,
  input  A,
  input  B,
  input  C,
  input  D,
  input  OUT
);

  wire and_1_out, and_2_out, and_3_out, and_4_out, or_1_out, or_2_out;

  and and_1 (and_1_out, ~E, A);  // AND_Gate
  and and_2 (and_2_out, E, B);
  and and_3 (and_3_out, ~W, C);  // AND_Gate
  and and_4 (and_4_out, W, D);
  or or_1 (or_1_out, and_1_out, and_2_out);
  or or_2 (or_2_out, and_3_out, and_4_out);
  or or_3 (OUT, or_1_out, or_2_out);
endmodule
